// Digital circuit pr04-1.dig as structural Verilog
module pr04_1 (
  input  A,
  input  B,
  input  C,
  input  D,
  input  LT,
  input  BI,
  input  RBI,
  input  dd,
  input  cc,
  input  bb,
  input  aa,
  input  ee,
  input  ff,
  input  gg
);

  wire _7448_1_pin9, _7448_1_pin10, _7448_1_pin11, _7448_1_pin12, _7448_1_pin13, _7448_1_pin14, _7448_1_pin15;

  _7448 _7448_1 (
    .pin1(B), .pin2(C), .pin3(LT), .pin4(BI), .pin5(RBI), .pin6(D), .pin7(A), .pin8(1'b0),
    .pin9(_7448_1_pin9), .pin10(_7448_1_pin10), .pin11(_7448_1_pin11), .pin12(_7448_1_pin12),
    .pin13(_7448_1_pin13), .pin14(_7448_1_pin14), .pin15(_7448_1_pin15), .pin16(1'b1));
  Seven_Seg #(.ledPersistence("true"), .commonConnectionType("anode")) seven_seg_1 (
    .a(_7448_1_pin13), .b(_7448_1_pin12), .c(_7448_1_pin11), .d(_7448_1_pin10), .e(_7448_1_pin9),
    .f(_7448_1_pin15), .g(_7448_1_pin14), .dp(1'b0));
  Seven_Seg seven_seg_2 (.a(aa), .b(bb), .c(cc), .d(dd), .e(ee), .f(ff), .g(gg), .dp(1'b0));
endmodule
