// Digital circuit pr04.dig as structural Verilog
module pr04 (
  input  A,
  input  B,
  input  C,
  input  D,
  input  nLT,
  input  nBI,
  input  nRBI,
  input  d_2,
  input  c_2,
  input  b_2,
  input  a_2,
  input  e,
  input  f,
  input  g,
  output h
);

  wire _7448_1_pin9, _7448_1_pin10, _7448_1_pin11, _7448_1_pin12, _7448_1_pin13, _7448_1_pin14, _7448_1_pin15;

  _7448 _7448_1 (
    .pin1(B), .pin2(C), .pin3(nLT), .pin4(nBI), .pin5(nRBI), .pin6(D), .pin7(A), .pin8(1'b0),
    .pin9(_7448_1_pin9), .pin10(_7448_1_pin10), .pin11(_7448_1_pin11), .pin12(_7448_1_pin12),
    .pin13(_7448_1_pin13), .pin14(_7448_1_pin14), .pin15(_7448_1_pin15), .pin16(1'b1));
  Seven_Seg #(.ledPersistence("true"), .commonConnectionType("anode")) seven_seg_1 (
    .a(_7448_1_pin13), .b(_7448_1_pin12), .c(_7448_1_pin11), .d(_7448_1_pin10), .e(_7448_1_pin9),
    .f(_7448_1_pin15), .g(_7448_1_pin14), .dp(1'b0));
  Seven_Seg seven_seg_2 (.a(a_2), .b(b_2), .c(c_2), .d(d_2), .e(e), .f(f), .g(g), .dp(1'b0));

  assign h = 1'b0;
endmodule
