// Digital circuit pr05_p1.dig as structural Verilog
module pr05_p1 (
  input  a_4,
  input  a_3,
  input  a_2,
  input  a_1,
  input  b_4,
  input  b_3,
  input  b_2,
  input  b_1,
  input  c_i,
  output s_4,
  output s_3,
  output s_2,
  output s_1,
  output c_o
);

  _74283 _74283_1 (
    .pin1(s_2), .pin2(b_2), .pin3(a_2), .pin4(s_1), .pin5(a_1), .pin6(b_1), .pin7(c_i), .pin8(1'b0),
    .pin9(c_o), .pin10(s_4), .pin11(b_4), .pin12(a_4), .pin13(s_3), .pin14(a_3), .pin15(b_3), .pin16(1'b1));
endmodule
