// Digital circuit pr06_p4.dig as structural Verilog
module pr06_p4 (
  input  clk
);

  wire and_1_out, jk_ff_as_1_nq, jk_ff_as_1_q, jk_ff_as_2_nq, jk_ff_as_2_q, jk_ff_as_3_nq, not_1_out;

  JK_FF_AS jk_ff_as_1 (.Set(1'b0), .J(1'b1), .C(clk), .K(1'b1), .Clr(and_1_out), .Q(jk_ff_as_1_q), .nQ(jk_ff_as_1_nq));
  LED q_1 (.in(jk_ff_as_2_nq));
  LED q_2 (.in(jk_ff_as_3_nq));
  LED q_0 (.in(jk_ff_as_1_nq));
  and and_1 (and_1_out, jk_ff_as_3_nq, not_1_out, jk_ff_as_1_nq);
  JK_FF_AS jk_ff_as_2 (
    .Set(1'b0), .J(1'b1), .C(jk_ff_as_1_q), .K(1'b1), .Clr(and_1_out), .Q(jk_ff_as_2_q), .nQ(jk_ff_as_2_nq));
  not not_1 (not_1_out, jk_ff_as_2_nq);
  JK_FF_AS jk_ff_as_3 (
    .Set(1'b0), .J(1'b1), .C(jk_ff_as_2_q), .K(1'b1), .Clr(and_1_out), .nQ(jk_ff_as_3_nq));  // open: Q

  // Notes on the sheet:
  //   clk: Hz: 2
endmodule
