// Digital circuit pr08.dig as structural Verilog
module pr08 (
  input  clk,
  input  pre
);

  wire and_1_out, and_2_out, and_3_out, and_4_out, d_0, d_1, d_2, nq_0, nq_1, nq_2, q_0, q_1, q_2;

  D_FF_AS u_Q_0 (.Set(pre), .D(d_0), .C(clk), .Clr(pre), .Q(q_0));  // open: nQ
  D_FF_AS u_Q_1 (.Set(pre), .D(d_1), .C(clk), .Clr(pre), .Q(q_1));  // open: nQ
  D_FF_AS u_Q_2 (.Set(pre), .D(d_2), .C(clk), .Clr(pre), .Q(q_2));  // open: nQ
  not not_1 (nq_0, q_0);
  not not_2 (nq_1, q_1);
  not not_3 (nq_2, q_2);
  and and_1 (and_1_out, nq_0, q_1);
  and and_2 (and_2_out, nq_1, nq_0);
  and and_3 (and_3_out, q_0, q_1, nq_2);
  and and_4 (and_4_out, nq_1, q_2);
  and and_5 (d_2, nq_1, q_0);
  or or_1 (d_0, nq_1, and_1_out);
  or or_2 (d_1, and_2_out, and_3_out, and_4_out);
  Seven_Seg_Hex seven_seg_hex_1 (.d({1'b0, q_2, q_1, q_0}), .dp(1'b0));
endmodule
